# Fritzing sketch Skematik (saved by Fritzing 0.9.3b)
breadboards: 1

parts:
  hc-sr1 = hc-sr04
  J1 = Basic Servo
  Part1 = Arduino Uno (Rev3)
  R1 = Rotary Potentiometer (Small) [maximum_resistance=100kΩ package=THT]
  J2 = Piezo Speaker
  Part2 = RFID-RC522-v3
  U1 = LIPO-2000mAh [package=lipo-2000]
  LED1 = smd LED [color="Red (633nm)" package="1206 [SMD]"]
  LED2 = smd LED [color="Red (633nm)" package="0805 [SMD]"]
  LCD1 = LCD screen
  R2 = Resistor [tolerance=±5% resistance=220 package="2010 [SMD]"]
  R3 = Resistor [tolerance=±5% resistance=220 package="2010 [SMD]"]

nets:
  VCC: hc-sr1.VCC, J1.vcc, Part1.VIN, R1.leg2, U1.+, LCD1.LED+
  N1: hc-sr1.Trig, Part1.D2
  N2: hc-sr1.Echo, Part1.D7
  GND: hc-sr1.GND, J1.gnd, R1.leg1, J2.pin1, U1.-, LED1.cathode, LED2.cathode, LCD1.LED-
  N3: J1.pulse, Part1.D8
  N4: Part1.A0, R1.wiper
  N5: Part1.A4/SDA, LCD1.RS
  N6: Part1.A5/SCL, LCD1.R/W
  N7: Part1.D9_PWM, Part2.RST
  N8: Part1.D10_PWM/SS, Part2.SDA
  N9: Part1.D11_PWM/MOSI, Part2.MISO
  N10: Part1.D12/MISO, Part2.MOSI
  N11: Part1.D13/SCK, Part2.SCK
  N12: Part1.D3_PWM, J2.pin2
  N13: Part1.D4, R3.Pin_1
  N14: Part1.D5_PWM, R2.Pin_1
  3V3: Part1.3V3, Part2.3.3V
  GND_2: Part1.GND, Part2.GND
  N15: LED1.anode, R3.Pin_0
  N16: LED2.anode, R2.Pin_0

custom parts:
  RFID-RC522-v3: A simple China made RFID-RC522 Reader (6x4 cm); do check the pin labels, as this is a MFRC522 based clone.
